// Logisim project ALU.circ as structural Verilog: 3 circuits, main circuit main
module main (
  input  A3,
  input  A2,
  input  A1,
  input  A0,
  input  B3,
  input  B2,
  input  B1,
  input  B0,
  input  C_IN,
  output S3,
  output S2,
  output S1,
  output S0,
  output C_OUT,
  output NEG,
  output ZERO
);

  wire and_1_out, and_2_out, not_1_out, not_2_out, not_3_out, not_4_out, xor_1_out, xor_2_out, xor_3_out,
       xor_4_out;

  xor xor_1 (xor_1_out, B3, C_IN);
  xor xor_2 (xor_2_out, B2, C_IN);
  xor xor_3 (xor_3_out, B1, C_IN);
  xor xor_4 (xor_4_out, B0, C_IN);
  _4_Bit_Adder u_4_bit_adder_1 (
    .A3(A3), .A2(A2), .A1(A1), .A0(A0), .B3(xor_1_out), .B2(xor_2_out), .B1(xor_3_out), .B0(xor_4_out),
    .C_IN(C_IN), .S3(NEG), .S2(S2), .S1(S1), .S0(S0), .C_OUT(C_OUT));
  not not_1 (not_1_out, S0);
  not not_2 (not_2_out, S1);
  not not_3 (not_3_out, S2);
  not not_4 (not_4_out, NEG);
  and and_1 (and_1_out, not_1_out, not_2_out);
  and and_2 (and_2_out, and_1_out, not_3_out);
  and and_3 (ZERO, and_2_out, not_4_out);

  assign S3 = NEG;
endmodule

module Full_Adder (
  input  IN_A,
  input  IN_B,
  input  C_IN,
  output SUM,
  output C_OUT
);

  wire and_1_out, and_2_out, xor_1_out;

  xor xor_1 (xor_1_out, IN_A, IN_B);
  and and_1 (and_1_out, IN_A, IN_B);
  xor xor_2 (SUM, xor_1_out, C_IN);
  and and_2 (and_2_out, xor_1_out, C_IN);
  or or_1 (C_OUT, and_2_out, and_1_out);
endmodule

module _4_Bit_Adder (
  input  A3,
  input  A2,
  input  A1,
  input  A0,
  input  B3,
  input  B2,
  input  B1,
  input  B0,
  input  C_IN,
  output S3,
  output S2,
  output S1,
  output S0,
  output C_OUT
);

  wire full_adder_1_c_out, full_adder_2_c_out, full_adder_3_c_out;

  Full_Adder full_adder_1 (.IN_A(A3), .IN_B(B3), .C_IN(C_IN), .SUM(S3), .C_OUT(full_adder_1_c_out));
  Full_Adder full_adder_2 (.IN_A(A2), .IN_B(B2), .C_IN(full_adder_1_c_out), .SUM(S2), .C_OUT(full_adder_2_c_out));
  Full_Adder full_adder_3 (.IN_A(A1), .IN_B(B1), .C_IN(full_adder_2_c_out), .SUM(S1), .C_OUT(full_adder_3_c_out));
  Full_Adder full_adder_4 (.IN_A(A0), .IN_B(B0), .C_IN(full_adder_3_c_out), .SUM(S0), .C_OUT(C_OUT));
endmodule
